// Logisim project full_adder.circ as structural Verilog
module full_adder (
  input  A,
  input  B,
  input  Cin,
  output Sum,
  output Cout
);

  wire P1, P2, X1;

  xor xor_1 (X1, A, B);
  and and_1 (P1, A, B);
  xor xor_2 (Sum, X1, Cin);
  and and_2 (P2, X1, Cin);
  or or_1 (Cout, P1, P2);
endmodule
